// Digital circuit ALU.dig as structural Verilog
module ALU (
  input  [7:0] From_B,
  input  [7:0] From_A,
  input  S_u,
  input  O_u,
  output [7:0] W_out,
  output Gt,
  output Eq,
  output Lt
);

  wire [7:0] add_1_s, multiplexer_1_out, sub_1_s;

  assign W_out = O_u ? multiplexer_1_out : 8'bz;  // Driver driver_1
  Multiplexer #(.Bits(8)) multiplexer_1 (.sel(S_u), .in_0(add_1_s), .in_1(sub_1_s), .out(multiplexer_1_out));
  Add #(.Bits(8)) add_1 (.a(From_B), .b(From_A), .c_i(1'b0), .s(add_1_s));  // open: c_o
  Sub #(.Bits(8)) sub_1 (.a(From_A), .b(From_B), .c_i(1'b0), .s(sub_1_s));  // open: c_o
  Comparator #(.Signed("true"), .Bits(8)) comparator_1 (.a(From_A), .b({8{1'b0}}), .gt(Gt), .eq(Eq), .lt(Lt));
endmodule
