// Digital circuit Accumulator.dig as structural Verilog
module Accumulator (
  input  [7:0] W_in,
  input  CLK,
  input  L_A,
  input  O_A,
  output [7:0] W_out,
  output [7:0] To_ALU
);

  assign W_out = O_A ? To_ALU : 8'bz;  // Driver driver_1
  Register #(.Bits(8)) register_1 (.D(W_in), .C(CLK), .en(L_A), .Q(To_ALU));
  // Pins of 1 and 8 bits meet at To_ALU
endmodule
