// Digital circuit B Register.dig as structural Verilog
module B_Register (
  input  [7:0] W_in,
  input  CLK,
  input  L_B,
  output [7:0] To_ALU
);

  Register #(.Bits(8)) register_1 (.D(W_in), .C(CLK), .en(L_B), .Q(To_ALU));
  // Pins of 1 and 8 bits meet at To_ALU
endmodule
