// Digital circuit Combined Memory.dig as structural Verilog
module Combined_Memory (
  input  CLK,
  input  [7:0] From_mar,
  input  [7:0] W_in,
  input  S_mem,
  input  L_RAM,
  input  O_mem,
  output [7:0] W_out
);

  wire [7:0] multiplexer_1_out, ramdualport_1_d, rom_1_d;

  ROM #(.AddrBits(8), .Bits(8)) rom_1 (.A(From_mar), .sel(1'b1), .D(rom_1_d));
  RAMDualPort #(.AddrBits(8), .Bits(8)) ramdualport_1 (
    .A(From_mar), .Din(W_in), .str(L_RAM), .C(CLK), .ld(S_mem), .D(ramdualport_1_d));
  Multiplexer #(.Bits(8)) multiplexer_1 (.sel(S_mem), .in_0(rom_1_d), .in_1(ramdualport_1_d), .out(multiplexer_1_out));
  assign W_out = O_mem ? multiplexer_1_out : 8'bz;  // Driver driver_1

  // Notes on the sheet:
  //   contents of rom_1 (hex, n*v repeats v):
  //   e0,30,e0,31,41,52,60,32,40,21,70,30,d4,42,80,90
endmodule
