// Digital circuit Flags.dig as structural Verilog
module Flags (
  input  Gt_ALU,
  input  Eq_ALU,
  input  Lt_ALU,
  input  Gt,
  input  Eq,
  input  Lt,
  output j
);

  wire and_1_out, and_2_out, and_3_out;

  and and_1 (and_1_out, Gt_ALU, Gt);
  and and_2 (and_2_out, Eq_ALU, Eq);
  and and_3 (and_3_out, Lt_ALU, Lt);
  or or_1 (j, and_1_out, and_2_out, and_3_out);
endmodule
