// Digital circuit Hex-to-dec-display.dig as structural Verilog
module Hex_to_dec_display (
  input  [7:0] in,
  output b1,
  output c1,
  output a1,
  output a2,
  output a3,
  output a4,
  output a5,
  output a6,
  output a7,
  output b2,
  output b3,
  output b4,
  output b5,
  output b6,
  output b7,
  output c2,
  output c3,
  output c4,
  output c5,
  output c6,
  output c7
);

  ROM #(.AddrBits(8), .Bits(7)) rom_1 (.A(in), .sel(1'b1), .D({a1, a2, a3, a4, a5, a6, a7}));
  ROM #(.AddrBits(8), .Bits(7)) rom_2 (.A(in), .sel(1'b1), .D({b1, b2, b3, b4, b5, b6, b7}));
  ROM #(.AddrBits(8), .Bits(7)) rom_3 (.A(in), .sel(1'b1), .D({c1, c2, c3, c4, c5, c6, c7}));

  // Notes on the sheet:
  //   contents of rom_1 (hex, n*v repeats v):
  //   100*7e,100*30,56*6d
  //   contents of rom_2 (hex, n*v repeats v):
  //   10*7e,10*30,10*6d,10*79,10*33,10*5b,10*5f,10*70,10*7f,10*7b,10*7e
  //   ,10*30,10*6d,10*79,10*33,10*5b,10*5f,10*70,10*7f,10*7b,10*7e,10*30
  //   ,10*6d,10*79,10*33,6*5b
  //   contents of rom_3 (hex, n*v repeats v):
  //   7e,30,6d,79,33,5b,5f,70,7f,7b,7e,30,6d,79,33,5b,5f,70,7f,7b,7e
  //   ,30,6d,79,33,5b,5f,70,7f,7b,7e,30,6d,79,33,5b,5f,70,7f,7b,7e,30
  //   ,6d,79,33,5b,5f,70,7f,7b,7e,30,6d,79,33,5b,5f,70,7f,7b,7e,30,6d
  //   ,79,33,5b,5f,70,7f,7b,7e,30,6d,79,33,5b,5f,70,7f,7b,7e,30,6d,79
  //   ,33,5b,5f,70,7f,7b,7e,30,6d,79,33,5b,5f,70,7f,7b,7e,30,6d,79,33
  //   ,5b,5f,70,7f,7b,7e,30,6d,79,33,5b,5f,70,7f,7b,7e,30,6d,79,33,5b
  //   ,5f,70,7f,7b,7e,30,6d,79,33,5b,5f,70,7f,7b,7e,30,6d,79,33,5b,5f
  //   ,70,7f,7b,7e,30,6d,79,33,5b,5f,70,7f,7b,7e,30,6d,79,33,5b,5f,70
  //   ,7f,7b,7e,30,6d,79,33,5b,5f,70,7f,7b,7e,30,6d,79,33,5b,5f,70,7f
  //   ,7b,7e,30,6d,79,33,5b,5f,70,7f,7b,7e,30,6d,79,33,5b,5f,70,7f,7b
  //   ,7e,30,6d,79,33,5b,5f,70,7f,7b,7e,30,6d,79,33,5b,5f,70,7f,7b,7e
  //   ,30,6d,79,33,5b,5f,70,7f,7b,7e,30,6d,79,33,5b,5f,70,7f,7b,7e,30
  //   ,6d,79,33,5b
endmodule
