// Digital circuit Incrementer.dig as structural Verilog
module Incrementer (
  input  [7:0] in,
  output [7:0] out
);

  Add #(.Bits(8)) add_1 (.a(in), .b(8'h1), .c_i(1'b0), .s(out));  // open: c_o
endmodule
