// Digital circuit Input Port 1.dig as structural Verilog
module Input_Port_1 (
  input  [15:0] KB_in,
  input  L_KB,
  input  O_KB,
  output [7:0] W_out
);

  wire [7:0] register_1_q, sub_1_s;

  Sub #(.Bits(8)) sub_1 (.a(KB_in[7:0]), .b(8'h30), .c_i(1'b0), .s(sub_1_s));  // open: c_o
  // Probe on sub_1_s
  Register #(.Bits(8)) register_1 (.D(sub_1_s), .C(L_KB), .en(1'b1), .Q(register_1_q));
  assign W_out = O_KB ? register_1_q : 8'bz;  // Driver driver_1
endmodule
