// Digital circuit Instruction Register.dig as structural Verilog
module Instruction_Register (
  input  [7:0] W_in,
  input  CLK,
  input  L_i,
  input  O_i,
  output [3:0] To_controller,
  output [7:0] W_out
);

  wire [3:0] register_1_q;

  Register #(.Bits(8)) register_1 (.D(W_in), .C(CLK), .en(L_i), .Q({To_controller, register_1_q}));
  assign W_out = O_i ? {4'b0000, register_1_q} : 8'bz;  // Driver driver_1
endmodule
