// Digital circuit MAR.dig as structural Verilog
module MAR (
  input  [7:0] W_in,
  input  L_m,
  input  CLK,
  output [7:0] To_mem
);

  Register #(.Bits(8)) register_1 (.D(W_in), .C(CLK), .en(L_m), .Q(To_mem));
endmodule
