// Digital circuit Output Register.dig as structural Verilog
module Output_Register (
  input  [7:0] W_in,
  input  CLK,
  input  L_O,
  output [7:0] To_display
);

  Register #(.Bits(8)) register_1 (.D(W_in), .C(CLK), .en(L_O), .Q(To_display));
endmodule
