// Digital circuit Program Counter.dig as structural Verilog
module Program_Counter (
  input  [7:0] W_in,
  input  CLK,
  input  j,
  input  O_pc,
  input  Inc,
  output [7:0] W_out
);

  wire or_1_out;
  wire [7:0] incrementer_1_out, multiplexer_1_out, multiplexer_2_out, register_1_q;

  or or_1 (or_1_out, Inc, j);
  Register #(.Bits(8)) register_1 (.D(multiplexer_1_out), .C(CLK), .en(or_1_out), .Q(register_1_q));
  Multiplexer #(.Bits(8)) multiplexer_1 (
    .sel(Inc), .in_0(multiplexer_2_out), .in_1(incrementer_1_out), .out(multiplexer_1_out));
  Incrementer incrementer_1 (.in(register_1_q), .out(incrementer_1_out));
  Multiplexer #(.Bits(8)) multiplexer_2 (.sel(j), .in_0({8{1'b0}}), .in_1(W_in), .out(multiplexer_2_out));
  assign W_out = O_pc ? register_1_q : 8'bz;  // Driver driver_1
endmodule
