// Digital circuit Ring Counter.dig as structural Verilog
module Ring_Counter (
  input  CLK,
  input  CLR,
  output T_1,
  output T_2,
  output T_3,
  output [2:0] T_n
);

  wire [2:0] counter_1_out;
  wire [7:3] lookuptable_1_out;

  Counter #(.Bits(3)) counter_1 (.en(CLK), .C(CLK), .clr(CLR), .out(counter_1_out));  // open: ovf
  LookUpTable #(.Bits(8)) lookuptable_1 (
    .in0(counter_1_out[0]), .in1(counter_1_out[1]), .in2(counter_1_out[2]),
    .out({lookuptable_1_out, T_3, T_2, T_1}));
  LookUpTable #(.Bits(3)) lookuptable_2 (
    .in0(lookuptable_1_out[3]), .in1(lookuptable_1_out[4]), .in2(lookuptable_1_out[5]),
    .in3(lookuptable_1_out[6]), .in4(lookuptable_1_out[7]), .out(T_n));

  // Notes on the sheet:
  //   contents of lookuptable_1 (hex, n*v repeats v):
  //   1,2,4,8,10,20,40,80
  //   contents of lookuptable_2 (hex, n*v repeats v):
  //   0,0,1,0,2,0,40,80,3,7*0,4,11*0,5
endmodule
